# Fritzing sketch GOOGLE smart home (saved by Fritzing 0.9.10b)
circuit board: 8.46667cm x 5.64444cm
breadboards: 1

parts:
  Mod1 = Amica NodeMCU DEVKIT 1.0
  Part1 = MQ-4
  KY-2 = Keyes Relay [package=THT]
  KY-3 = Keyes Relay [package=THT]
  Part2 = Lilypad Battery Connect  # not connected
  VCC1 = Battery block 9V
  J1 = Piezo Speaker  # not connected
  U1 = Voltage Regulator [package=to220-adj]
  U2 = Luxeon LED [package=luxeon]
  M1 = DC Motor [voltage_(max)=6V voltage_(min)=3V]

nets:
  N1: Mod1.pin1, Mod1.pin_10
  N2: Mod1.pin2, Mod1.pin_9
  N3: Mod1.pin_13, KY-3.power
  N4: Mod1.pin_14, KY-2.power
  N5: Mod1.pin_16, Part1.VCC
  N6: Part1.GND, KY-2.signal, KY-3.signal, VCC1.-, U1.IN
  N7: Part1.AO, KY-3.ground, U1.OUT
  N8: KY-2.NO, KY-3.C, KY-3.NO, U2.S, M1.pin_1
  N9: VCC1.+, U1.ADJ
  N10: U2.C, M1.pin_2

notes:
  GND
  Relay To Control Fans
  Relay To Control Lights
  VCC
  BUZZER
  MQ4 Gas Sensor
  Battery
  LM7805 Regulator
  AC Supply
  Ac Light
  AC Fan

custom parts:
  Keyes Relay: The Keyes 5V relay module is suitable for SCM development, home appliance control. It uses a 5V~12V TIL control signal which can control DC / AC signal.
